// Digital circuit ALU.dig as structural Verilog
module ALU (
  input  [7:0] A,
  input  [7:0] B,
  input  SU,
  input  EO,
  output [7:0] out,
  output carry,
  output zero
);

  wire add_2_c_o, and_1_out, and_2_out, nor_1_out, nor_2_out, nor_3_out, nor_4_out;
  wire [3:0] add_1_s, add_2_s, xor_1_out;
  wire [7:4] xor_1_out_2;

  assign {xor_1_out_2, xor_1_out} = B ^ {8{SU}};  // XOr xor_1, 8 bits wide
  Add #(.Bits(4)) add_1 (.a(A[7:4]), .b(xor_1_out_2), .c_i(add_2_c_o), .s(add_1_s), .c_o(carry));
  Add #(.Bits(4)) add_2 (.a(A[3:0]), .b(xor_1_out), .c_i(SU), .s(add_2_s), .c_o(add_2_c_o));
  // NOr nor_1 has open pins: In_1=open, In_2=open, out=nor_1_out
  // NOr nor_2 has open pins: In_1=open, In_2=open, out=nor_2_out
  // NOr nor_3 has open pins: In_1=open, In_2=open, out=nor_3_out
  // NOr nor_4 has open pins: In_1=open, In_2=open, out=nor_4_out
  assign out = EO ? {add_1_s, add_2_s} : 8'bz;  // Driver driver_1
  and and_1 (and_1_out, nor_1_out, nor_2_out);
  and and_2 (and_2_out, nor_3_out, nor_4_out);
  // And and_3 has open pins: In_1=and_1_out, In_2=and_2_out, out=open
endmodule
