// Digital circuit PC.dig as structural Verilog
module PC (
  input  CE,
  input  clk,
  input  [11:0] IN,
  input  J,
  output [11:0] OUT
);

  CounterPreset #(.Bits(12)) counterpreset_1 (
    .en(CE), .C(clk), .dir(1'b0), .in(IN), .ld(J), .clr(1'b0), .out(OUT));  // open: ovf
endmodule
