// Digital circuit uINST.dig as structural Verilog
module uINST (
  input  nclk,
  input  [3:0] OP,
  input  [11:0] ARG,
  input  eql,
  input  carry,
  input  zero,
  output [7:0] DATA,
  output [11:0] ADDR,
  output CE,
  output J,
  output PO,
  output II,
  output ROMO,
  output RAMI,
  output RAMO,
  output SU,
  output EO,
  output BI,
  output BO,
  output AI,
  output AO,
  output [3:0] GFX,
  output EXT0,
  output EXT1,
  output [3:0] MC
);

  wire [3:0] counter_1_out;
  wire [7:4] eeprom_3_d;

  Counter #(.Bits(4)) counter_1 (.en(1'b1), .C(nclk), .clr(eeprom_3_d[7]), .out(counter_1_out));  // open: ovf
  EEPROM #(.AddrBits(11), .Bits(8)) eeprom_1 (
    .A({eql, carry, zero, counter_1_out, OP}), .CS(1'b1), .WE(1'b0), .OE(1'b1),
    .D({SU, RAMO, RAMI, ROMO, II, PO, J, CE}));
  EEPROM #(.AddrBits(11), .Bits(8)) eeprom_2 (
    .A({eql, carry, zero, counter_1_out, OP}), .CS(1'b1), .WE(1'b0), .OE(1'b1),
    .D({MC[2:0], AO, AI, BO, BI, EO}));
  EEPROM #(.AddrBits(11), .Bits(8)) eeprom_3 (
    .A({eql, carry, zero, counter_1_out, OP}), .CS(1'b1), .WE(1'b0), .OE(1'b1),
    .D({eeprom_3_d, EXT1, EXT0, GFX[0], MC[3]}));
  assign DATA = eeprom_3_d[4] ? ARG[7:0] : 8'bz;  // Driver driver_1
  assign ADDR = eeprom_3_d[5] ? ARG : 12'bz;  // Driver driver_2
  assign ADDR = eeprom_3_d[6] ? {ARG[11:4], 4'b0111} : 12'bz;  // Driver driver_3
  // Pins of 1 and 4 bits meet at MC
  // Pins of 1 and 4 bits meet at GFX
endmodule
