// Digital circuit main.dig as structural Verilog
module main (
  input  clk
);

  wire AI, AO, BI, BO, carry, CE, clk_t, EO, EQL, EXT, GFX, HLT, II, J, MC, nand_1_out, nand_2_out, nclk, PO,
       RAMI, RAMO, ROMO, SU, zero;
  wire [3:0] reg_inst_1_op;
  wire [7:0] DATA, ramdualport_1_d, reg_a_1_a, reg_b_1_b;
  wire [11:0] ADDR, MEMADDR, pc_1_out, reg_inst_1_arg;
  wire [15:0] IR;

  MAR mar_1 (.ADDR(ADDR), .clk(clk_t), .MC(MC), .MEM(MEMADDR));
  REG_INST reg_inst_1 (.ii(II), .clk(clk_t), .INST(IR), .ARG(reg_inst_1_arg), .OP(reg_inst_1_op));
  PC pc_1 (.CE(CE), .clk(clk_t), .J(J), .IN(ADDR), .OUT(pc_1_out));
  EEPROM #(.AddrBits(11), .Bits(8)) ROM_A (.A(MEMADDR[10:0]), .CS(1'b1), .WE(1'b0), .OE(1'b1), .D(IR[7:0]));
  EEPROM #(.AddrBits(11), .Bits(8)) ROM_B (.A(MEMADDR[10:0]), .CS(1'b1), .WE(1'b0), .OE(1'b1), .D(IR[15:8]));
  assign DATA = ROMO ? IR[7:0] : 8'bz;  // Driver driver_1
  assign ADDR = PO ? pc_1_out : 12'bz;  // Driver driver_2
  // uINST uinst_1: pin names not known; wires that end beside it: reg_inst_1_op, reg_inst_1_arg, nclk, zero, carry, EQL, CE, J, PO, II, ROMO, RAMI, RAMO, SU, EO, DATA, BI, ADDR, BO, AI, AO, MC, HLT, GFX, EXT
  RAMDualPort #(.AddrBits(4), .Bits(8)) ramdualport_1 (
    .A(MEMADDR[3:0]), .Din(DATA), .str(RAMI), .C(clk_t), .ld(1'b1), .D(ramdualport_1_d));
  nand nand_1 (nand_1_out, HLT, HLT);
  assign DATA = RAMO ? ramdualport_1_d : 8'bz;  // Driver driver_3
  nand nand_2 (nand_2_out, nand_1_out, clk);
  nand nand_3 (clk_t, nand_2_out, nand_2_out);
  REG_A reg_a_1 (.clk(clk_t), .AI(AI), .AO(AO), .A(reg_a_1_a), .BUS_i(DATA), .BUS_o(DATA));
  ALU alu_1 (.A(reg_a_1_a), .B(reg_b_1_b), .SU(SU), .EO(EO), .out(DATA), .carry(carry), .zero(zero), .EQL(EQL));
  REG_B reg_b_1 (.BUS_i(DATA), .BUS_o(DATA), .clk(clk_t), .BI(BI), .BO(BO), .B(reg_b_1_b));
  nand nand_4 (nclk, clk_t, clk_t);
  // GFX gfx_1: pin names not known; wires that end beside it: GFX, DATA, clk_t

  // Notes on the sheet:
  //   clk: Hz: 5
endmodule
